// Logisim project adder-1.circ as structural Verilog
module Adder_Sub_4 (
  input  [3:0] in_1,
  input  [3:0] in_2,
  output OVERFLOW,
  output OVERFLOW_2,
  output [3:0] out_5,
  output [3:0] out_6
);

  adder_4 adder_4_1 (.OVERFLOW(OVERFLOW), .out_4(out_5), .in_2(in_2), .in_1(in_1));
  Sub_4 sub_4_1 (.in_1(in_1), .out_3(OVERFLOW_2), .in_2(in_2), .out_4(out_6));
endmodule

module adder_4 (
  input  [3:0] in_1,
  input  [3:0] in_2,
  output OVERFLOW,
  output [3:0] out_4
);

  wire adder_1_2_c_out, adder_1_3_c_out, adder_1_4_c_out;

  Adder_1 adder_1_1 (.A(in_2[3]), .B(in_1[3]), .C_in(adder_1_2_c_out), .S(out_4[3]), .C_out(OVERFLOW));
  Adder_1 adder_1_2 (.A(in_2[2]), .B(in_1[2]), .C_in(adder_1_3_c_out), .S(out_4[2]), .C_out(adder_1_2_c_out));
  Adder_1 adder_1_3 (.A(in_2[1]), .B(in_1[1]), .C_in(adder_1_4_c_out), .S(out_4[1]), .C_out(adder_1_3_c_out));
  Adder_1 adder_1_4 (.A(in_2[0]), .B(in_1[0]), .C_in(1'b0), .S(out_4[0]), .C_out(adder_1_4_c_out));
endmodule

module Adder_1 (
  input  A,
  input  B,
  input  C_in,
  output S,
  output C_out
);

  wire and_1_out, and_2_out, xor_1_out;

  xor xor_1 (xor_1_out, A, B);
  and and_1 (and_1_out, B, A);
  and and_2 (and_2_out, C_in, xor_1_out);
  xor xor_2 (S, xor_1_out, C_in);
  or or_1 (C_out, and_2_out, and_1_out);
endmodule

module Sub_4 (
  input  [3:0] in_1,
  input  [3:0] in_2,
  output out_3,
  output [3:0] out_4
);

  wire sub_1_2_c_out, sub_1_3_c_out, sub_1_4_c_out;

  Sub_1 sub_1_1 (.A(in_1[3]), .B(in_2[3]), .S(out_4[3]), .C_in(sub_1_2_c_out), .C_out(out_3));
  Sub_1 sub_1_2 (.A(in_1[2]), .B(in_2[2]), .S(out_4[2]), .C_in(sub_1_3_c_out), .C_out(sub_1_2_c_out));
  Sub_1 sub_1_3 (.A(in_1[1]), .B(in_2[1]), .S(out_4[1]), .C_in(sub_1_4_c_out), .C_out(sub_1_3_c_out));
  Sub_1 sub_1_4 (.A(in_1[0]), .B(in_2[0]), .S(out_4[0]), .C_in(1'b0), .C_out(sub_1_4_c_out));
endmodule

module Sub_1 (
  input  A,
  input  B,
  input  C_in,
  output S,
  output C_out
);

  wire and_1_out, and_2_out, not_1_out, not_2_out, xor_1_out;

  not not_1 (not_1_out, A);
  xor xor_1 (xor_1_out, A, B);
  not not_2 (not_2_out, xor_1_out);
  and and_1 (and_1_out, B, not_1_out);
  and and_2 (and_2_out, C_in, not_2_out);
  xor xor_2 (S, xor_1_out, C_in);
  or or_1 (C_out, and_2_out, and_1_out);
endmodule
